# Fritzing sketch monitor-diagram (saved by Fritzing 0.9.3b)
breadboards: 1

parts:
  Part1 = Photon
  S1 = Momentary Switch [package=ksa_sealed_tac_switch]
  S2 = Pushbutton [package="[THT]"]
  LED1 = LED - 5mm [color="Yellow (592nm)" package="5 mm [THT]"]
  R1 = Resistor [tolerance=±5% resistance=220 package="2512 [SMD]"]

nets:
  N1: Part1.A0, S1.4
  N2: Part1.A5, LED1.anode
  N3: Part1.GND, S2.Pin_4, R1.Pin_1
  N4: Part1.D4, S2.Pin_2
  N5: S1.2, LED1.cathode, R1.Pin_0

notes:
  Confirmation Button
  Print Bed Button
  Confirmation LED
